// Logisim project Encoder.circ as structural Verilog: 1 circuit, main circuit main
module main (
  input  in_1,
  input  in_2,
  input  in_3,
  input  in_4
);

  wire or_1_out, or_2_out;

  or or_1 (or_1_out, in_1, in_2);
  or or_2 (or_2_out, in_1, in_3);
  LED led_1 (.in(or_1_out));
  LED led_2 (.in(or_2_out));
endmodule
